# Fritzing sketch circuitDisagram (saved by Fritzing 0.9.4)
breadboards: 1

parts:
  Bauteil1 = Arduino Nano (Rev3.0)
  Bauteil2 = InvenSense MPU6050
  LED1 = smd LED [color="Red (633nm)" package="0805 [SMD]"]
  R1 = Resistor [tolerance=±5% resistance=220 package="2512 [SMD]"]

nets:
  GND: Bauteil1.GND, Bauteil2.GND, LED1.cathode
  N1: Bauteil1.D4, R1.Pin_1
  5V: Bauteil1.5V, Bauteil2.VCC
  N2: Bauteil1.A5, Bauteil2.SCL
  N3: Bauteil1.A4, Bauteil2.SDA
  N4: LED1.anode, R1.Pin_0
